# Fritzing sketch Arhitectura sistemuluiREC (saved by Fritzing 0.9.4)
perfboards: 2

parts:
  VALVE1 = Plastic Solenoid Valve
  Part1 = LCD1602-I2C
  U5 = RF-LINK_RX [package=rf-link_rx]
  KY-3 = Keyes Relay [package=THT]
  U6 = ESP8266 NodeMCU LoLin base
  KY-4 = Keyes Relay [package=THT]
  U7 = RF-LINK_TX [package=rf-link_tx]
  D3 = Diode [package=diode-hv]  # not connected
  IC1 = Hex Inverter Schmitt Trigger SN74HC14 [package="DIP (Dual Inline)"]
  S3 = Momentary Switch [package=ksa_sealed_tac_switch]
  S4 = Momentary Switch [package=ksa_sealed_tac_switch]
  Part4 = Arduino MicroSD Shield
  R2 = Resistor [tolerance=±5% resistance=10k package="0603 [SMD]"]
  C1 = Electrolytic Capacitor [capacitance=1µF package="1010 [SMD, electrolytic]"]
  R3 = Resistor [tolerance=±5% resistance=10k package="0603 [SMD]"]
  R4 = Resistor [tolerance=±5% resistance=10k package="0603 [SMD]"]
  C2 = Electrolytic Capacitor [capacitance=1µF package="1010 [SMD, electrolytic]"]
  R5 = Resistor [tolerance=±5% resistance=10k package="0603 [SMD]"]
  DHT11_1 = DHT11 module
  V1 = DC Power [voltage=5]  # not connected
  Part6 = Arduino Uno (Rev3)
  IC2 = Hex Inverter Schmitt Trigger SN74HC14 [package="DIP (Dual Inline)"]
  S5 = Momentary Switch [package=ksa_sealed_tac_switch]
  S6 = Momentary Switch [package=ksa_sealed_tac_switch]
  U8 = ESP8266 NodeMCU LoLin base
  VALVE2 = Plastic Solenoid Valve
  KY-5 = Keyes Relay [package=THT]
  Part7 = LCD1602-I2C
  U9 = RF-LINK_TX [package=rf-link_tx]
  D4 = Diode [package=diode-hv]  # not connected
  R6 = Resistor [tolerance=±5% resistance=10k package="0603 [SMD]"]
  R7 = Resistor [tolerance=±5% resistance=10k package="0603 [SMD]"]
  R8 = Resistor [tolerance=±5% resistance=10k package="0603 [SMD]"]
  R9 = Resistor [tolerance=±5% resistance=10k package="0603 [SMD]"]
  C3 = Electrolytic Capacitor [capacitance=1µF package="1010 [SMD, electrolytic]"]
  C4 = Electrolytic Capacitor [capacitance=1µF package="1010 [SMD, electrolytic]"]
  DHT11_2 = DHT11 module

nets:
  N1: VALVE1.no_name_yet, KY-4.C
  GND: Part1.GND, U6.GND1-0, U6.GND1-1, U6.GND1-2, U6.GND3-2, U6.GND8-4, U6.GND8-5, U6.GND8-10, U6.GND8-11, U7.GND, DHT11_1.GND
  VCC: Part1.VCC, U6.D0-2, U6.D0-3, U6.VIN, U6.5V-0, U6.5V-1, DHT11_1.VCC, DHT11_1.DATA
  N2: Part1.SDA, U6.D2-2, U6.D2-3
  N3: Part1.SCL, U6.D1-3
  GND_2: U5.GND, KY-3.ground, Part6.GND
  N4: U5.DATA, Part6.D4
  N5: KY-3.signal, Part6.D7
  N6: KY-3.power, Part6.5V
  N7: U6.3V1-0, U6.3V1-1, U6.3V1-2, R3.Pin_0
  N8: U6.D3-0, U6.D3-1, U6.D3-2, KY-4.signal
  N9: U6.D5-0, U6.D5-3, IC1.3Y
  N10: U6.D6-0, U6.D6-3, IC1.4Y
  N11: U6.D7-0, U6.D7-1, U6.D7-2, U7.DATA
  N12: U6.UI-2, U6.UI-3, U7.ANT, U7.+5V
  N13: IC1.3A, R2.Pin_1, C1.+
  N14: IC1.GND, S4.1, C1.-, C2.-
  N15: IC1.4A, R4.Pin_1, C2.+
  N16: S3.3, R3.Pin_1, R4.Pin_0
  N17: S4.3, R2.Pin_0, R5.Pin_1
  N18: Part4.N$52, Part4.N$88
  N19: Part4.N$89, Part4.N$143
  N20: IC2.3A, R6.Pin_1, C3.+
  N21: IC2.3Y, U8.D5-0, U8.D5-3
  N22: IC2.GND, S6.1, C3.-, C4.-
  N23: IC2.4Y, U8.D6-0, U8.D6-3
  N24: IC2.4A, R8.Pin_1, C4.+
  N25: S5.3, R7.Pin_1, R8.Pin_0
  N26: S6.3, R6.Pin_0, R9.Pin_1
  GND_3: U8.GND1-0, U8.GND1-1, U8.GND1-2, U8.GND3-2, U8.GND8-4, U8.GND8-5, U8.GND8-6, U8.GND8-10, U8.GND8-11, Part7.GND, U9.GND, DHT11_2.GND
  N27: U8.3V1-0, U8.3V1-1, U8.3V1-2, R7.Pin_0
  VCC_2: U8.D0-2, U8.D0-3, U8.VIN, U8.5V-0, U8.5V-1, Part7.VCC, DHT11_2.VCC, DHT11_2.DATA
  N28: U8.D1-3, Part7.SCL
  N29: U8.D2-2, U8.D2-3, Part7.SDA
  N30: U8.D3-0, U8.D3-1, U8.D3-2, U8.D3-3, U8.D4-0, U8.D4-2, KY-5.signal
  N31: U8.D7-0, U8.D7-1, U8.D7-2, U9.DATA
  N32: U8.UI-2, U8.UI-3, U9.ANT, U9.+5V
  N33: VALVE2.no_name_yet, KY-5.C

notes:
  Alimentator 12 V

custom parts:
  LCD1602-I2C: A standard character display, usually with 2x16 characters. Comes in many colors with LCM1602 IIC attached.
  Keyes Relay: The Keyes 5V relay module is suitable for SCM development, home appliance control. It uses a 5V~12V TIL control signal which can control DC / AC signal.
  ESP8266 NodeMCU LoLin base: ESP8266 based NodeMCU Base
  DHT11 module: DHT11 black pcb module
