# Fritzing sketch Arhitectura sistemuluiREC (saved by Fritzing 0.9.4)
perfboards: 2

parts:
  U5 = RF-LINK_RX [package=rf-link_rx]
  KY-3 = Keyes Relay [package=THT]
  Part4 = Arduino MicroSD Shield
  V1 = DC Power [voltage=5]  # not connected
  Part6 = Arduino Uno (Rev3)
  IC2 = Hex Inverter Schmitt Trigger SN74HC14 [package="DIP (Dual Inline)"]
  S5 = Momentary Switch [package=ksa_sealed_tac_switch]
  S6 = Momentary Switch [package=ksa_sealed_tac_switch]
  U8 = ESP8266 NodeMCU LoLin base
  VALVE2 = Plastic Solenoid Valve
  KY-5 = Keyes Relay [package=THT]
  Part7 = LCD1602-I2C
  U9 = RF-LINK_TX [package=rf-link_tx]
  D4 = Diode [package=diode-hv]  # not connected
  R6 = Resistor [tolerance=±5% resistance=10k package="0603 [SMD]"]
  R7 = Resistor [tolerance=±5% resistance=10k package="0603 [SMD]"]
  R8 = Resistor [tolerance=±5% resistance=10k package="0603 [SMD]"]
  R9 = Resistor [tolerance=±5% resistance=10k package="0603 [SMD]"]
  C3 = Electrolytic Capacitor [capacitance=1µF package="1010 [SMD, electrolytic]"]
  C4 = Electrolytic Capacitor [capacitance=1µF package="1010 [SMD, electrolytic]"]
  DHT11_2 = DHT11 module
  IC3 = Hex Inverter Schmitt Trigger SN74HC14 [package="DIP (Dual Inline)"]
  S7 = Momentary Switch [package=ksa_sealed_tac_switch]
  S8 = Momentary Switch [package=ksa_sealed_tac_switch]
  U10 = ESP8266 NodeMCU LoLin base
  VALVE3 = Plastic Solenoid Valve
  KY-6 = Keyes Relay [package=THT]
  Part8 = LCD1602-I2C
  U11 = RF-LINK_TX [package=rf-link_tx]
  D5 = Diode [package=diode-hv]  # not connected
  R10 = Resistor [tolerance=±5% resistance=10k package="0603 [SMD]"]
  R11 = Resistor [tolerance=±5% resistance=10k package="0603 [SMD]"]
  R12 = Resistor [tolerance=±5% resistance=10k package="0603 [SMD]"]
  R13 = Resistor [tolerance=±5% resistance=10k package="0603 [SMD]"]
  C5 = Electrolytic Capacitor [capacitance=1µF package="1010 [SMD, electrolytic]"]
  C6 = Electrolytic Capacitor [capacitance=1µF package="1010 [SMD, electrolytic]"]
  DHT11_3 = DHT11 module

nets:
  GND: U5.GND, KY-3.ground, Part6.GND
  N1: U5.DATA, Part6.D4
  N2: KY-3.signal, Part6.D7
  N3: KY-3.power, Part6.5V
  N4: Part4.N$52, Part4.N$88
  N5: Part4.N$89, Part4.N$143
  N6: IC2.3A, R6.Pin_1, C3.+
  N7: IC2.3Y, U8.D5-0, U8.D5-3
  N8: IC2.GND, S6.1, C3.-, C4.-
  N9: IC2.4Y, U8.D6-0, U8.D6-3
  N10: IC2.4A, R8.Pin_1, C4.+
  N11: S5.3, R7.Pin_1, R8.Pin_0
  N12: S6.3, R6.Pin_0, R9.Pin_1
  GND_2: U8.GND1-0, U8.GND1-1, U8.GND1-2, U8.GND3-2, U8.GND8-4, U8.GND8-5, U8.GND8-10, U8.GND8-11, Part7.GND, U9.GND, DHT11_2.GND
  N13: U8.3V1-0, U8.3V1-1, U8.3V1-2, R7.Pin_0
  N14: U8.D0-2, U8.D0-3, DHT11_2.DATA
  N15: U8.D1-3, Part7.SCL
  N16: U8.D2-2, U8.D2-3, Part7.SDA
  N17: U8.D3-0, U8.D3-1, U8.D3-2, U8.D3-3, U8.D4-0, U8.D4-2, KY-5.signal
  N18: U8.D7-0, U8.D7-1, U8.D7-2, U9.DATA
  VCC: U8.VIN, U8.5V-0, U8.5V-1, Part7.VCC, DHT11_2.VCC
  N19: U8.UI-2, U8.UI-3, U9.ANT, U9.+5V
  N20: VALVE2.no_name_yet, KY-5.C
  N21: IC3.3A, R10.Pin_1, C5.+
  GND_3: IC3.3Y, U10.GND1-0, U10.GND1-1, U10.GND1-2, U10.3V1-0, U10.3V1-1, U10.3V1-2, U10.3V2-0, U10.GND2-0, U10.D5-0, U10.D5-3, U10.GND3-2, U10.GND8-4, U10.GND8-5, U10.GND8-9, U10.GND8-11, Part8.GND, U11.GND, R11.Pin_0, DHT11_3.GND
  N22: IC3.GND, S8.1, C5.-, C6.-
  N23: IC3.4Y, U10.D6-0, U10.D6-3
  N24: IC3.4A, R12.Pin_1, C6.+
  N25: S7.3, R11.Pin_1, R12.Pin_0
  N26: S8.3, R10.Pin_0, R13.Pin_1
  N27: U10.D0-2, U10.D0-3, U10.D1-2, U10.D1-3, Part8.SCL, DHT11_3.DATA
  N28: U10.D2-2, U10.D2-3, Part8.SDA
  N29: U10.D3-0, U10.D3-1, U10.D3-2, U10.D3-3, U10.D4-0, U10.D4-2, KY-6.signal
  N30: U10.D7-0, U10.D7-1, U10.D7-2, U11.DATA
  VCC_2: U10.VIN, U10.5V-0, U10.5V-1, Part8.VCC, DHT11_3.VCC
  N31: U10.UI-2, U10.UI-3, U11.ANT, U11.+5V
  N32: VALVE3.no_name_yet, KY-6.C

custom parts:
  Keyes Relay: The Keyes 5V relay module is suitable for SCM development, home appliance control. It uses a 5V~12V TIL control signal which can control DC / AC signal.
  ESP8266 NodeMCU LoLin base: ESP8266 based NodeMCU Base
  LCD1602-I2C: A standard character display, usually with 2x16 characters. Comes in many colors with LCM1602 IIC attached.
  DHT11 module: DHT11 black pcb module
